# Fritzing sketch wanderer-a3s1 (saved by Fritzing 0.9.3b)
circuit board: 6.19478cm x 5.2705cm
breadboards: 1

parts:
  Digital_Pins = female pin header, 8 pins [form="♀ (female)"]
  Analog_Pins = female pin header, 6 pins [form="♀ (female)"]  # not connected
  GND_and_Power = female pin header, 8 pins [form="♀ (female)"]
  More_Digital_Pins = female pin header, 10 pins [form="♀ (female)"]
  R4 = Resistor [tolerance=±5% resistance=330 package=THT]
  R5 = Resistor [tolerance=±5% resistance=330 package=THT]
  R6 = Resistor [tolerance=±5% resistance=330 package=THT]
  J1 = female pin header, 4 pins [form="♀ (female)"]
  J2 = female pin header, 4 pins [form="♀ (female)"]
  Bluefruit_SPI_Friend1 = female pin header, 9 pins [form="♀ (female)"]
  J4 = screw terminal, 2 pins
  SW2 = female pin header, 3 pins [form="♀ (female)"]

nets:
  N1: Digital_Pins.pin4, R4.Pin_0
  N2: Digital_Pins.pin5, Bluefruit_SPI_Friend1.pin3
  N3: Digital_Pins.pin6, R5.Pin_0
  N4: Digital_Pins.pin7, R6.Pin_0
  N5: Digital_Pins.pin8, Bluefruit_SPI_Friend1.pin5
  N6: GND_and_Power.pin4, Bluefruit_SPI_Friend1.pin1
  N7: More_Digital_Pins.pin1, Bluefruit_SPI_Friend1.pin6
  N8: More_Digital_Pins.pin4, Bluefruit_SPI_Friend1.pin7
  N9: More_Digital_Pins.pin5, Bluefruit_SPI_Friend1.pin8
  N10: More_Digital_Pins.pin6, Bluefruit_SPI_Friend1.pin9
  N11: More_Digital_Pins.pin7, J1.pin2, J2.pin2, Bluefruit_SPI_Friend1.pin2
  N12: R4.Pin_1, J1.pin1, J2.pin1
  N13: R5.Pin_1, J1.pin3, J2.pin3
  N14: R6.Pin_1, J1.pin4, J2.pin4
  N15: J4.pin1, SW2.pin2
  N16: J4.pin2, SW2.pin3

notes:
  5V servo
  signal
  GND
