# Fritzing sketch wanderer-a3s2 (saved by Fritzing 0.9.3b)
circuit board: 3.59604cm x 5.26505cm
breadboards: 1

parts:
  GND_and_Power = female pin header, 8 pins [form="♀ (female)"]
  R4 = Resistor [tolerance=±5% resistance=330 package=THT]
  R5 = Resistor [tolerance=±5% resistance=330 package=THT]
  R6 = Resistor [tolerance=±5% resistance=330 package=THT]
  J1 = female pin header, 4 pins [form="♀ (female)"]
  J2 = female pin header, 4 pins [form="♀ (female)"]
  Bluefruit_SPI_Friend1 = female pin header, 9 pins [form="♀ (female)"]
  J4 = screw terminal, 2 pins
  More_Digital_Pins = female pin header, 7 pins [form="♀ (female)"]
  Analog_Pins = female pin header, 4 pins [form="♀ (female)"]  # not connected
  Digital_Pins = female pin header, 6 pins [form="♀ (female)"]
  SW2 = female pin header, 3 pins [form="♀ (female)"]

nets:
  N1: GND_and_Power.pin4, Bluefruit_SPI_Friend1.pin1
  N2: R4.Pin_0, Digital_Pins.pin2
  N3: R4.Pin_1, J1.pin1, J2.pin1
  N4: R5.Pin_0, Digital_Pins.pin4
  N5: R5.Pin_1, J1.pin3, J2.pin3
  N6: R6.Pin_0, Digital_Pins.pin5
  N7: R6.Pin_1, J1.pin4, J2.pin4
  N8: J1.pin2, J2.pin2, Bluefruit_SPI_Friend1.pin2, More_Digital_Pins.pin7
  N9: Bluefruit_SPI_Friend1.pin3, Digital_Pins.pin3
  N10: Bluefruit_SPI_Friend1.pin5, Digital_Pins.pin6
  N11: Bluefruit_SPI_Friend1.pin6, More_Digital_Pins.pin1
  N12: Bluefruit_SPI_Friend1.pin7, More_Digital_Pins.pin4
  N13: Bluefruit_SPI_Friend1.pin8, More_Digital_Pins.pin5
  N14: Bluefruit_SPI_Friend1.pin9, More_Digital_Pins.pin6
  N15: J4.pin1, SW2.pin3
  N16: J4.pin2, SW2.pin2

notes:
  5V servo
  signal
  GND
