# Fritzing sketch controller-trial01 (saved by Fritzing 0.9.3b)
circuit board: 6.88566cm x 5.36311cm
breadboards: 1

parts:
  XBee_Left = female pin header, 11 pins [form="♀ (female)"]
  XBee_Right = female pin header, 11 pins [form="♀ (female)"]  # not connected
  Arduino = Arduino Uno (Rev3)
  Wanderer_Joystick = Thumb Joystick
  Navigator_Joystick = Thumb Joystick
  W_calibration_+ = Pushbutton [package="[THT]"]
  W_calibration_- = Pushbutton [package="[THT]"]
  N_calibration_+ = Pushbutton [package="[THT]"]
  N_calibration_- = Pushbutton [package="[THT]"]
  W_fan = Pushbutton [package="[THT]"]
  N_message_- = Pushbutton [package="[THT]"]
  N_message_+ = Pushbutton [package="[THT]"]
  W_unison_mode = Pushbutton [package="[THT]"]
  N_play = Pushbutton [package="[THT]"]
  R1 = Resistor [tolerance=±5% resistance=10k package=THT]
  R2 = Resistor [tolerance=±5% resistance=10k package=THT]
  R3 = Resistor [tolerance=±5% resistance=10k package=THT]
  R4 = Resistor [tolerance=±5% resistance=10k package=THT]
  R5 = Resistor [tolerance=±5% resistance=10k package=THT]
  R6 = Resistor [tolerance=±5% resistance=10k package=THT]
  R7 = Resistor [tolerance=±5% resistance=10k package=THT]
  R8 = Resistor [tolerance=±5% resistance=10k package=THT]
  R9 = Resistor [tolerance=±5% resistance=10k package=THT]

nets:
  GND: XBee_Left.pin1, Arduino.GND, Wanderer_Joystick.GND, Navigator_Joystick.GND, R1.Pin_0, R2.Pin_0, R3.Pin_0, R4.Pin_0, R5.Pin_0, R6.Pin_0, R7.Pin_0, R8.Pin_0, R9.Pin_0
  N1: XBee_Left.pin2, Arduino.3V3
  N2: XBee_Left.pin3, Arduino.D2
  N3: XBee_Left.pin4, Arduino.D3_PWM
  N4: Arduino.A0, Wanderer_Joystick.HORZ
  N5: Arduino.A1, Wanderer_Joystick.VERT
  N6: Arduino.A2, Navigator_Joystick.HORZ
  N7: Arduino.A3, Navigator_Joystick.VERT
  N8: Arduino.D8, N_play.Pin_3, N_play.Pin_4, R5.Pin_1
  N9: Arduino.D9_PWM, W_calibration_+.Pin_3, W_calibration_+.Pin_4, R6.Pin_1
  N10: Arduino.D10_PWM/SS, W_calibration_-.Pin_3, W_calibration_-.Pin_4, R7.Pin_1
  N11: Arduino.D11_PWM/MOSI, N_calibration_+.Pin_3, N_calibration_+.Pin_4, R8.Pin_1
  N12: Arduino.D12/MISO, N_calibration_-.Pin_3, N_calibration_-.Pin_4, R9.Pin_1
  N13: Arduino.D4, W_fan.Pin_3, W_fan.Pin_4, R1.Pin_1
  N14: Arduino.D5_PWM, W_unison_mode.Pin_3, W_unison_mode.Pin_4, R2.Pin_1
  N15: Arduino.D6_PWM, N_message_+.Pin_3, N_message_+.Pin_4, R3.Pin_1
  N16: Arduino.D7, N_message_-.Pin_3, N_message_-.Pin_4, R4.Pin_1
  VCC: Arduino.5V, Wanderer_Joystick.VCC, Navigator_Joystick.VCC, W_calibration_+.Pin_1, W_calibration_+.Pin_2, W_calibration_-.Pin_1, N_calibration_+.Pin_1, N_calibration_-.Pin_1, N_calibration_-.Pin_2, W_fan.Pin_1, W_fan.Pin_2, N_message_-.Pin_1, N_message_+.Pin_1, N_message_+.Pin_2, W_unison_mode.Pin_1, N_play.Pin_1

notes:
  5V servo
  signal
  GND
  3.3V
  Ard P2
  Ard P3
