# Fritzing sketch controller-trial02-assuming-using-wires (saved by Fritzing 0.9.3b)
circuit board: 6.88566cm x 5.36311cm
breadboards: 1

parts:
  XBee_Left = female pin header, 11 pins [form="♀ (female)"]
  XBee_Right = female pin header, 11 pins [form="♀ (female)"]  # not connected
  R1 = Resistor [tolerance=±5% resistance=10k package=THT]
  R2 = Resistor [tolerance=±5% resistance=10k package=THT]
  W_Joystick = female pin header, 5 pins [form="♀ (female)"]
  N_Joystick = female pin header, 5 pins [form="♀ (female)"]
  WB1 = female pin header, 3 pins [form="♀ (female)"]
  WB2 = female pin header, 3 pins [form="♀ (female)"]
  R3 = Resistor [tolerance=±5% resistance=10k package=THT]
  NB1 = female pin header, 3 pins [form="♀ (female)"]
  R4 = Resistor [tolerance=±5% resistance=10k package=THT]
  NB2 = female pin header, 3 pins [form="♀ (female)"]
  R5 = Resistor [tolerance=±5% resistance=10k package=THT]
  NB3 = female pin header, 3 pins [form="♀ (female)"]
  R6 = Resistor [tolerance=±5% resistance=10k package=THT]
  WB3 = female pin header, 3 pins [form="♀ (female)"]
  R7 = Resistor [tolerance=±5% resistance=10k package=THT]
  WB4 = female pin header, 3 pins [form="♀ (female)"]
  R8 = Resistor [tolerance=±5% resistance=10k package=THT]
  NB4 = female pin header, 3 pins [form="♀ (female)"]
  R9 = Resistor [tolerance=±5% resistance=10k package=THT]
  NB5 = female pin header, 3 pins [form="♀ (female)"]
  Arduino = Arduino Uno (Rev3)

nets:
  N1: XBee_Left.pin1, R1.Pin_0, R2.Pin_0, W_Joystick.pin1, N_Joystick.pin1, R3.Pin_0, R4.Pin_0, R5.Pin_0, R6.Pin_0, R7.Pin_0, R8.Pin_0, R9.Pin_0, Arduino.GND
  N2: XBee_Left.pin2, Arduino.3V3
  N3: XBee_Left.pin3, Arduino.D2
  N4: XBee_Left.pin4, Arduino.D3_PWM
  N5: R1.Pin_1, WB1.pin3
  N6: R2.Pin_1, WB2.pin3
  N7: W_Joystick.pin3, Arduino.A1
  N8: W_Joystick.pin4, Arduino.A0
  N9: W_Joystick.pin5, N_Joystick.pin5, WB1.pin1, WB2.pin1, NB1.pin1, NB2.pin1, NB3.pin1, WB3.pin1, WB4.pin1, NB4.pin1, NB5.pin1, Arduino.5V
  N10: N_Joystick.pin3, Arduino.A3
  N11: N_Joystick.pin4, Arduino.A2
  N12: WB1.pin2, Arduino.D4
  N13: WB2.pin2, Arduino.D5_PWM
  N14: R3.Pin_1, NB1.pin3
  N15: NB1.pin2, Arduino.D6_PWM
  N16: R4.Pin_1, NB2.pin3
  N17: NB2.pin2, Arduino.D7
  N18: R5.Pin_1, NB3.pin3
  N19: NB3.pin2, Arduino.D8
  N20: R6.Pin_1, WB3.pin3
  N21: WB3.pin2, Arduino.D9_PWM
  N22: R7.Pin_1, WB4.pin3
  N23: WB4.pin2, Arduino.D10_PWM/SS
  N24: R8.Pin_1, NB4.pin3
  N25: NB4.pin2, Arduino.D11_PWM/MOSI
  N26: R9.Pin_1, NB5.pin3
  N27: NB5.pin2, Arduino.D12/MISO

notes:
  5V servo
  signal
  GND
  3.3V
  Ard P2
  Ard P3
  SEL
  Y
  X
  5V
