# Fritzing sketch controller-trial03-weird schematic (saved by Fritzing 0.9.3b)
circuit board: 6.88566cm x 5.36311cm
breadboards: 1

parts:
  XBee_Left = female pin header, 11 pins [form="♀ (female)"]
  XBee_Right = female pin header, 11 pins [form="♀ (female)"]  # not connected
  R1 = Resistor [tolerance=±5% resistance=10k package=THT]
  R2 = Resistor [tolerance=±5% resistance=10k package=THT]
  R3 = Resistor [tolerance=±5% resistance=10k package=THT]
  R4 = Resistor [tolerance=±5% resistance=10k package=THT]
  R5 = Resistor [tolerance=±5% resistance=10k package=THT]
  R7 = Resistor [tolerance=±5% resistance=10k package=THT]
  R8 = Resistor [tolerance=±5% resistance=10k package=THT]
  R9 = Resistor [tolerance=±5% resistance=10k package=THT]
  5V = female pin header, 11 pins [form="♀ (female)"]
  GND = female pin header, 11 pins [form="♀ (female)"]
  R6 = Resistor [tolerance=±5% resistance=10k package=THT]
  WB1 = female pin header, 1 pin [form="♀ (female)"]
  WB2 = female pin header, 1 pin [form="♀ (female)"]
  NB1 = female pin header, 1 pin [form="♀ (female)"]
  NB2 = female pin header, 1 pin [form="♀ (female)"]
  NB3 = female pin header, 1 pin [form="♀ (female)"]
  WB3 = female pin header, 1 pin [form="♀ (female)"]
  WB4 = female pin header, 1 pin [form="♀ (female)"]
  NB4 = female pin header, 1 pin [form="♀ (female)"]
  W_Joystick = female pin header, 2 pins [form="♀ (female)"]
  N_Joystick = female pin header, 2 pins [form="♀ (female)"]
  Arduino = Arduino Uno (Rev3)
  NB5 = female pin header, 1 pin [form="♀ (female)"]

nets:
  N1: XBee_Left.pin1, R1.Pin_0, R2.Pin_0, R3.Pin_0, R4.Pin_0, R5.Pin_0, R7.Pin_0, R8.Pin_0, R9.Pin_0, GND.pin10, GND.pin11, R6.Pin_0, Arduino.GND
  N2: XBee_Left.pin2, Arduino.3V3
  N3: XBee_Left.pin3, Arduino.D2
  N4: XBee_Left.pin4, Arduino.D3_PWM
  N5: R1.Pin_1, GND.pin1
  N6: R2.Pin_1, GND.pin2
  N7: R3.Pin_1, GND.pin3
  N8: R4.Pin_1, GND.pin4
  N9: R5.Pin_1, GND.pin5
  N10: R7.Pin_1, GND.pin7
  N11: R8.Pin_1, GND.pin8
  N12: R9.Pin_1, GND.pin9
  N13: 5V.pin1, 5V.pin2, 5V.pin3, 5V.pin4, 5V.pin5, 5V.pin6, 5V.pin7, 5V.pin8, 5V.pin9, 5V.pin10, 5V.pin11, Arduino.5V
  N14: GND.pin6, R6.Pin_1
  N15: WB1.pin1, Arduino.D4
  N16: WB2.pin1, Arduino.D5_PWM
  N17: NB1.pin1, Arduino.D6_PWM
  N18: NB2.pin1, Arduino.D7
  N19: NB3.pin1, Arduino.D8
  N20: WB3.pin1, Arduino.D9_PWM
  N21: WB4.pin1, Arduino.D10_PWM/SS
  N22: NB4.pin1, Arduino.D11_PWM/MOSI
  N23: W_Joystick.pin1, Arduino.A1
  N24: W_Joystick.pin2, Arduino.A0
  N25: N_Joystick.pin1, Arduino.A3
  N26: N_Joystick.pin2, Arduino.A2
  N27: Arduino.D12/MISO, NB5.pin1

notes:
  5V servo
  signal
  GND
  3.3V
  Ard P2
  Ard P3
  Y
  X
