# Fritzing sketch controller-trial04-extra-buttons-and-pots (saved by Fritzing 0.9.3b)
circuit board: 6.88566cm x 5.36311cm
breadboards: 1

parts:
  XBee_Right = female pin header, 11 pins [form="♀ (female)"]  # not connected
  R1 = Resistor [tolerance=±5% resistance=10k package=THT]
  R2 = Resistor [tolerance=±5% resistance=10k package=THT]
  R3 = Resistor [tolerance=±5% resistance=10k package=THT]
  R4 = Resistor [tolerance=±5% resistance=10k package=THT]
  R5 = Resistor [tolerance=±5% resistance=10k package=THT]
  R7 = Resistor [tolerance=±5% resistance=10k package=THT]
  R8 = Resistor [tolerance=±5% resistance=10k package=THT]
  R9 = Resistor [tolerance=±5% resistance=10k package=THT]
  R6 = Resistor [tolerance=±5% resistance=10k package=THT]
  WB1 = female pin header, 1 pin [form="♀ (female)"]
  WB2 = female pin header, 1 pin [form="♀ (female)"]
  NB1 = female pin header, 1 pin [form="♀ (female)"]
  NB2 = female pin header, 1 pin [form="♀ (female)"]
  NB3 = female pin header, 1 pin [form="♀ (female)"]
  WB3 = female pin header, 1 pin [form="♀ (female)"]
  WB4 = female pin header, 1 pin [form="♀ (female)"]
  NB4 = female pin header, 1 pin [form="♀ (female)"]
  W_Joystick = female pin header, 2 pins [form="♀ (female)"]
  N_Joystick = female pin header, 2 pins [form="♀ (female)"]
  Arduino = Arduino Uno (Rev3)
  NB5 = female pin header, 1 pin [form="♀ (female)"]
  R10 = Resistor [tolerance=±5% resistance=220 package=THT]
  5V = female pin header, 14 pins [form="♀ (female)"]
  Pot1 = female pin header, 1 pin [form="♀ (female)"]
  Pot2 = female pin header, 1 pin [form="♀ (female)"]
  EB1 = female pin header, 1 pin [form="♀ (female)"]
  GND = female pin header, 15 pins [form="♀ (female)"]
  XBee_Left = female pin header, 11 pins [form="♀ (female)"]

nets:
  N1: R1.Pin_0, R2.Pin_0, R3.Pin_0, R4.Pin_0, R5.Pin_0, R7.Pin_0, R8.Pin_0, R9.Pin_0, R6.Pin_0, Arduino.GND, R10.Pin_0, GND.pin11, GND.pin12, GND.pin13, GND.pin14, GND.pin15, XBee_Left.pin1
  N2: R1.Pin_1, GND.pin1
  N3: R2.Pin_1, GND.pin2
  N4: R3.Pin_1, GND.pin3
  N5: R4.Pin_1, GND.pin4
  N6: R5.Pin_1, GND.pin5
  N7: R7.Pin_1, GND.pin7
  N8: R8.Pin_1, GND.pin8
  N9: R9.Pin_1, GND.pin9
  N10: R6.Pin_1, GND.pin6
  N11: WB1.pin1, Arduino.D4
  N12: WB2.pin1, Arduino.D5_PWM
  N13: NB1.pin1, Arduino.D6_PWM
  N14: NB2.pin1, Arduino.D7
  N15: NB3.pin1, Arduino.D8
  N16: WB3.pin1, Arduino.D9_PWM
  N17: WB4.pin1, Arduino.D10_PWM/SS
  N18: NB4.pin1, Arduino.D11_PWM/MOSI
  N19: W_Joystick.pin1, Arduino.A1
  N20: W_Joystick.pin2, Arduino.A0
  N21: N_Joystick.pin1, Arduino.A3
  N22: N_Joystick.pin2, Arduino.A2
  N23: Arduino.A4/SDA, Pot1.pin1
  N24: Arduino.A5/SCL, Pot2.pin1
  N25: Arduino.D12/MISO, NB5.pin1
  N26: Arduino.D13/SCK, EB1.pin1
  N27: Arduino.D2, XBee_Left.pin3
  N28: Arduino.D3_PWM, XBee_Left.pin4
  N29: Arduino.3V3, XBee_Left.pin2
  N30: Arduino.5V, 5V.pin1, 5V.pin2, 5V.pin3, 5V.pin4, 5V.pin5, 5V.pin6, 5V.pin7, 5V.pin8, 5V.pin9, 5V.pin10, 5V.pin11, 5V.pin12, 5V.pin13, 5V.pin14
  N31: R10.Pin_1, GND.pin10

notes:
  5V servo
  signal
  GND
  3.3V
  Ard P2
  Ard P3
  Y
  X
  LT
  RT
