# Fritzing sketch navigator-trial01 (saved by Fritzing 0.9.3b)
circuit board: 6.88566cm x 5.36311cm
breadboards: 1

parts:
  J1 = Camdenboss CTB0158-2 [part_number=CTB0158-2 package=THT]
  Sliding_Toggle_Switch = Toggle Switch [package=THT]
  Servo_P9 = female pin header, 3 pins [form="♀ (female)"]
  Servo_P10 = female pin header, 3 pins [form="♀ (female)"]
  XBee_Left = female pin header, 11 pins [form="♀ (female)"]
  XBee_Right = female pin header, 11 pins [form="♀ (female)"]  # not connected
  Arduino = Arduino Uno (Rev3)

nets:
  GND: J1.pin1, Servo_P9.pin3, Servo_P10.pin3, XBee_Left.pin1, Arduino.GND
  N1: J1.pin2, Sliding_Toggle_Switch.L1
  N2: Sliding_Toggle_Switch.COM, Servo_P9.pin2, Servo_P10.pin2
  N3: Servo_P9.pin1, Arduino.D9_PWM
  N4: Servo_P10.pin1, Arduino.D10_PWM/SS
  N5: XBee_Left.pin2, Arduino.3V3
  N6: XBee_Left.pin3, Arduino.D2
  N7: XBee_Left.pin4, Arduino.D3_PWM
  5V: Arduino.5V

notes:
  Signal Pin 9
  5V Servo
  5V servo
  signal
  GND
  Signal Pin 10
  3.3V
  Ard P2
  Ard P3
