# Fritzing sketch navigator-trial02-assuming-motor-shield (saved by Fritzing 0.9.3b)
circuit board: 6.88566cm x 5.36311cm
breadboards: 1

parts:
  XBee_Left = female pin header, 11 pins [form="♀ (female)"]
  XBee_Right = female pin header, 11 pins [form="♀ (female)"]  # not connected
  Arduino = Arduino Uno (Rev3)

nets:
  GND: XBee_Left.pin1, Arduino.GND
  N1: XBee_Left.pin2, Arduino.3V3
  N2: XBee_Left.pin3, Arduino.D2
  N3: XBee_Left.pin4, Arduino.D3_PWM
  5V: Arduino.5V

notes:
  5V servo
  signal
  GND
  3.3V
  Ard P2
  Ard P3
