# Fritzing sketch xbee-trial01-only-xbee (saved by Fritzing 0.9.3b)
circuit board: 3.12076cm x 2.56775cm
breadboards: 1

parts:
  XBee_Left = female pin header, 11 pins [form="♀ (female)"]
  XBee_Right = female pin header, 11 pins [form="♀ (female)"]  # not connected
  Connectors_for_Arduino = female pin header, 4 pins [form="♀ (female)"]

nets:
  N1: XBee_Left.pin1, Connectors_for_Arduino.pin1
  N2: XBee_Left.pin2, Connectors_for_Arduino.pin2
  N3: XBee_Left.pin3, Connectors_for_Arduino.pin3
  N4: XBee_Left.pin4, Connectors_for_Arduino.pin4

notes:
  5V servo
  signal
  GND
  3.3V
  Ard P2
  Ard P3
