# Fritzing sketch xbee-trial02-half-shield-effect (saved by Fritzing 0.9.3b)
circuit board: 4.3348cm x 5.29689cm
breadboards: 1

parts:
  XBee_Left = female pin header, 11 pins [form="♀ (female)"]
  XBee_Right = female pin header, 11 pins [form="♀ (female)"]  # not connected
  Digital_Pins = female pin header, 8 pins [form="♀ (female)"]
  Analog_Pins = female pin header, 6 pins [form="♀ (female)"]  # not connected
  GND_and_Power = female pin header, 8 pins [form="♀ (female)"]
  More_Digital_Pins = female pin header, 10 pins [form="♀ (female)"]  # not connected

nets:
  N1: XBee_Left.pin1, GND_and_Power.pin2
  N2: XBee_Left.pin2, GND_and_Power.pin5
  N3: XBee_Left.pin3, Digital_Pins.pin3
  N4: XBee_Left.pin4, Digital_Pins.pin4

notes:
  5V servo
  signal
  GND
  3.3V
  Ard P2
  Ard P3
